// Logisim project main.circ as structural Verilog
module high_register (
  input  in_1,
  input  [7:0] in_2,
  input  in_3,
  output [7:0] out_4
);

  wire [7:0] d_ff_1_q;

  D_Flip_Flop #(.trigger("high")) d_ff_1 (.clk(in_1), .D(in_2[0]), .Q(d_ff_1_q[0]));  // open: Qn, preset, en, reset
  D_Flip_Flop #(.trigger("high")) d_ff_2 (.clk(in_1), .D(in_2[1]), .Q(d_ff_1_q[1]));  // open: Qn, preset, en, reset
  D_Flip_Flop #(.trigger("high")) d_ff_3 (.clk(in_1), .D(in_2[2]), .Q(d_ff_1_q[2]));  // open: Qn, preset, en, reset
  D_Flip_Flop #(.trigger("high")) d_ff_4 (.clk(in_1), .D(in_2[3]), .Q(d_ff_1_q[3]));  // open: Qn, preset, en, reset
  D_Flip_Flop #(.trigger("high")) d_ff_5 (.clk(in_1), .D(in_2[4]), .Q(d_ff_1_q[4]));  // open: Qn, preset, en, reset
  D_Flip_Flop #(.trigger("high")) d_ff_6 (.clk(in_1), .D(in_2[5]), .Q(d_ff_1_q[5]));  // open: Qn, preset, en, reset
  D_Flip_Flop #(.trigger("high")) d_ff_7 (.clk(in_1), .D(in_2[6]), .Q(d_ff_1_q[6]));  // open: Qn, preset, en, reset
  D_Flip_Flop #(.trigger("high")) d_ff_8 (.clk(in_1), .D(in_2[7]), .Q(d_ff_1_q[7]));  // open: Qn, preset, en, reset
  Pull_Resistor pull_resistor_1 (.node(in_3));
  assign out_4 = in_3 ? d_ff_1_q : 8'bz;  // Controlled_Buffer controlled_buffer_1
endmodule

module low_register (
  input  in_1,
  input  in_2,
  input  [7:0] in_3,
  input  in_4,
  input  in_5,
  output [7:0] out_6,
  output [7:0] out_7,
  output [7:0] out_8
);

  wire nand_1_out;

  nand nand_1 (nand_1_out, in_1, in_2);
  Pull_Resistor pull_resistor_1 (.node(in_3));
  D_Flip_Flop #(.trigger("low")) d_ff_1 (
    .clk(nand_1_out), .D(in_3[0]), .Q(out_6[0]), .reset(in_5));  // open: Qn, preset, en
  D_Flip_Flop #(.trigger("low")) d_ff_2 (
    .clk(nand_1_out), .D(in_3[1]), .Q(out_6[1]), .reset(in_5));  // open: Qn, preset, en
  D_Flip_Flop #(.trigger("low")) d_ff_3 (
    .clk(nand_1_out), .D(in_3[2]), .Q(out_6[2]), .reset(in_5));  // open: Qn, preset, en
  D_Flip_Flop #(.trigger("low")) d_ff_4 (
    .clk(nand_1_out), .D(in_3[3]), .Q(out_6[3]), .reset(in_5));  // open: Qn, preset, en
  D_Flip_Flop #(.trigger("low")) d_ff_5 (
    .clk(nand_1_out), .D(in_3[4]), .Q(out_6[4]), .reset(in_5));  // open: Qn, preset, en
  D_Flip_Flop #(.trigger("low")) d_ff_6 (
    .clk(nand_1_out), .D(in_3[5]), .Q(out_6[5]), .reset(in_5));  // open: Qn, preset, en
  D_Flip_Flop #(.trigger("low")) d_ff_7 (
    .clk(nand_1_out), .D(in_3[6]), .Q(out_6[6]), .reset(in_5));  // open: Qn, preset, en
  D_Flip_Flop #(.trigger("low")) d_ff_8 (
    .clk(nand_1_out), .D(in_3[7]), .Q(out_6[7]), .reset(in_5));  // open: Qn, preset, en
  assign out_7 = in_4 ? out_6 : 8'bz;  // Controlled_Buffer controlled_buffer_1
  Pull_Resistor pull_resistor_2 (.node(in_4));
  assign out_8 = in_4 ? {8{1'b1}} : 8'bz;  // Controlled_Buffer controlled_buffer_2
endmodule

module Instruction_Pointer (
  input  in_1,
  input  in_2,
  input  [7:0] in_3,
  input  [7:0] HIGH,
  input  in_5,
  input  in_6,
  input  in_7,
  output [15:0] out_8,
  output [7:0] LOW,
  output [7:0] HIGH_2
);

  wire n2_bit_counter_1_out_9, n2_bit_counter_2_out_9, n2_bit_counter_3_out_9, n2_bit_counter_4_out_9,
       n2_bit_counter_5_out_9, n2_bit_counter_6_out_9, n2_bit_counter_7_out_9;

  _2_bit_counter u_2_bit_counter_1 (
    .clk(in_1), .enable(in_2), .d1(in_3[0]), .d2(in_3[1]), .inp_count(in_6), .reset(in_7), .out_7(out_8[0]),
    .out_8(out_8[1]), .out_9(n2_bit_counter_1_out_9));
  _2_bit_counter u_2_bit_counter_2 (
    .clk(in_1), .enable(n2_bit_counter_1_out_9), .d1(in_3[2]), .d2(in_3[3]), .inp_count(in_6), .reset(in_7),
    .out_7(out_8[2]), .out_8(out_8[3]), .out_9(n2_bit_counter_2_out_9));
  _2_bit_counter u_2_bit_counter_3 (
    .clk(in_1), .enable(n2_bit_counter_2_out_9), .d1(in_3[4]), .d2(in_3[5]), .inp_count(in_6), .reset(in_7),
    .out_7(out_8[4]), .out_8(out_8[5]), .out_9(n2_bit_counter_3_out_9));
  _2_bit_counter u_2_bit_counter_4 (
    .clk(in_1), .enable(n2_bit_counter_3_out_9), .d1(in_3[6]), .d2(in_3[7]), .inp_count(in_6), .reset(in_7),
    .out_7(out_8[6]), .out_8(out_8[7]), .out_9(n2_bit_counter_4_out_9));
  _2_bit_counter u_2_bit_counter_5 (
    .clk(in_1), .enable(n2_bit_counter_4_out_9), .d1(HIGH[0]), .d2(HIGH[1]), .inp_count(in_6), .reset(in_7),
    .out_7(out_8[8]), .out_8(out_8[9]), .out_9(n2_bit_counter_5_out_9));
  _2_bit_counter u_2_bit_counter_6 (
    .clk(in_1), .enable(n2_bit_counter_5_out_9), .d1(HIGH[2]), .d2(HIGH[3]), .inp_count(in_6), .reset(in_7),
    .out_7(out_8[10]), .out_8(out_8[11]), .out_9(n2_bit_counter_6_out_9));
  _2_bit_counter u_2_bit_counter_7 (
    .clk(in_1), .enable(n2_bit_counter_6_out_9), .d1(HIGH[4]), .d2(HIGH[5]), .inp_count(in_6), .reset(in_7),
    .out_7(out_8[12]), .out_8(out_8[13]), .out_9(n2_bit_counter_7_out_9));
  _2_bit_counter u_2_bit_counter_8 (
    .clk(in_1), .enable(n2_bit_counter_7_out_9), .d1(HIGH[6]), .d2(HIGH[7]), .inp_count(in_6), .reset(in_7),
    .out_7(out_8[14]), .out_8(out_8[15]));  // open: out_9
  assign LOW = in_5 ? out_8[7:0] : 8'bz;  // Controlled_Buffer controlled_buffer_1
  assign HIGH_2 = in_5 ? out_8[15:8] : 8'bz;  // Controlled_Buffer controlled_buffer_2

  // Notes on the sheet:
  //   LOW
endmodule

module _2_bit_counter (
  input  clk,
  input  enable,
  input  d1,
  input  d2,
  input  inp_count,
  input  reset,
  output out_7,
  output out_8,
  output out_9
);

  wire and_1_out, and_2_out, d_ff_1_qn, multiplexer_1_out, multiplexer_2_out, or_1_out, xor_1_out;

  and and_1 (and_1_out, inp_count, clk);
  or or_1 (or_1_out, and_1_out, and_2_out);
  and and_2 (and_2_out, clk, enable);
  Multiplexer #(.enable("false")) multiplexer_1 (.in0(d_ff_1_qn), .in1(d1), .out(multiplexer_1_out), .sel(inp_count));
  D_Flip_Flop #(.trigger("falling")) d_ff_1 (
    .clk(or_1_out), .D(multiplexer_1_out), .Q(out_7), .Qn(d_ff_1_qn), .reset(reset));  // open: preset, en
  xor xor_1 (xor_1_out, out_7, out_8);
  Multiplexer #(.enable("false")) multiplexer_2 (.in0(xor_1_out), .in1(d2), .out(multiplexer_2_out), .sel(inp_count));
  D_Flip_Flop #(.trigger("falling")) d_ff_2 (
    .clk(or_1_out), .D(multiplexer_2_out), .Q(out_8), .reset(reset));  // open: Qn, preset, en
  and and_3 (out_9, out_7, enable, out_8);
endmodule

module ALU (
  input  [7:0] in_1,
  input  clk,
  input  [7:0] in_3,
  input  [8:0] in_4,
  output [7:0] LOW,
  output [1:0] out_6,
  output [7:0] HIGH
);

  wire cf, not_1_out, not_2_out, not_3_out, zf;
  wire [7:0] and_1_out, full_adder_8bit_1_out_3, high_register_1_out_4, multiplexer_2_out, multiplexer_3_out,
       pull_resistor_2_node, xnor_1_out, xnor_9_out, xnor_17_out;

  Pull_Resistor pull_resistor_1 (.node(in_4));
  Pull_Resistor pull_resistor_2 (.node(pull_resistor_2_node));
  Multiplexer #(.width(8), .enable("false")) multiplexer_1 (
    .in0(in_1), .in1({8{1'b0}}), .out(pull_resistor_2_node), .sel(in_4[0]));
  Multiplexer #(.width(8), .enable("false")) multiplexer_2 (
    .in0(in_3), .in1({8{1'b0}}), .out(multiplexer_2_out), .sel(in_4[2]));
  Pull_Resistor pull_resistor_3 (.node(multiplexer_2_out));
  not not_1 (not_1_out, in_4[1]);
  not not_2 (not_2_out, in_4[3]);
  xnor xnor_1 (xnor_1_out[0], pull_resistor_2_node[0], not_1_out);
  xnor xnor_2 (xnor_1_out[1], pull_resistor_2_node[1], not_1_out);
  xnor xnor_3 (xnor_1_out[2], pull_resistor_2_node[2], not_1_out);
  xnor xnor_4 (xnor_1_out[3], pull_resistor_2_node[3], not_1_out);
  xnor xnor_5 (xnor_1_out[4], pull_resistor_2_node[4], not_1_out);
  xnor xnor_6 (xnor_1_out[5], pull_resistor_2_node[5], not_1_out);
  xnor xnor_7 (xnor_1_out[6], pull_resistor_2_node[6], not_1_out);
  xnor xnor_8 (xnor_1_out[7], pull_resistor_2_node[7], not_1_out);
  xnor xnor_9 (xnor_9_out[0], multiplexer_2_out[0], not_2_out);
  xnor xnor_10 (xnor_9_out[1], multiplexer_2_out[1], not_2_out);
  xnor xnor_11 (xnor_9_out[2], multiplexer_2_out[2], not_2_out);
  xnor xnor_12 (xnor_9_out[3], multiplexer_2_out[3], not_2_out);
  xnor xnor_13 (xnor_9_out[4], multiplexer_2_out[4], not_2_out);
  xnor xnor_14 (xnor_9_out[5], multiplexer_2_out[5], not_2_out);
  xnor xnor_15 (xnor_9_out[6], multiplexer_2_out[6], not_2_out);
  xnor xnor_16 (xnor_9_out[7], multiplexer_2_out[7], not_2_out);
  full_adder_8bit full_adder_8bit_1 (.in_1(xnor_1_out), .in_2(xnor_9_out), .out_3(full_adder_8bit_1_out_3), .out_4(cf));
  assign and_1_out = xnor_1_out & xnor_9_out;  // AND_Gate and_1, 8 bits wide
  Multiplexer #(.width(8), .enable("false")) multiplexer_3 (
    .in0(full_adder_8bit_1_out_3), .in1(and_1_out), .out(multiplexer_3_out), .sel(in_4[4]));
  not not_3 (not_3_out, in_4[5]);
  xnor xnor_17 (xnor_17_out[0], multiplexer_3_out[0], not_3_out);
  xnor xnor_18 (xnor_17_out[1], multiplexer_3_out[1], not_3_out);
  xnor xnor_19 (xnor_17_out[2], multiplexer_3_out[2], not_3_out);
  xnor xnor_20 (xnor_17_out[3], multiplexer_3_out[3], not_3_out);
  xnor xnor_21 (xnor_17_out[4], multiplexer_3_out[4], not_3_out);
  xnor xnor_22 (xnor_17_out[5], multiplexer_3_out[5], not_3_out);
  xnor xnor_23 (xnor_17_out[6], multiplexer_3_out[6], not_3_out);
  xnor xnor_24 (xnor_17_out[7], multiplexer_3_out[7], not_3_out);
  nor nor_1 (zf, xnor_17_out[0], xnor_17_out[1], xnor_17_out[2], xnor_17_out[3], xnor_17_out[4], xnor_17_out[5], xnor_17_out[6], xnor_17_out[7]);
  high_register high_register_1 (.in_1(clk), .in_2(xnor_17_out), .in_3(1'b1), .out_4(high_register_1_out_4));
  assign HIGH = in_4[8] ? high_register_1_out_4 : 8'bz;  // Controlled_Buffer controlled_buffer_1
  assign LOW = in_4[6] ? high_register_1_out_4 : 8'bz;  // Controlled_Buffer controlled_buffer_2
  D_Flip_Flop #(.trigger("falling")) d_ff_1 (.clk(in_4[7]), .D(zf), .Q(out_6[0]));  // open: Qn, preset, en, reset
  D_Flip_Flop #(.trigger("falling")) d_ff_2 (.clk(in_4[7]), .D(cf), .Q(out_6[1]));  // open: Qn, preset, en, reset
endmodule

module full_adder (
  input  in_1,
  input  in_2,
  input  in_3,
  output out_4,
  output out_5
);

  wire nor_1_out, nor_2_out, xnor_1_out;

  nor nor_1 (nor_1_out, in_1, in_2);
  xnor xnor_1 (xnor_1_out, in_1, in_2);
  nor nor_2 (nor_2_out, xnor_1_out, in_3);
  xnor xnor_2 (out_4, xnor_1_out, in_3);
  nor nor_3 (out_5, nor_1_out, nor_2_out);
endmodule

module full_adder_8bit (
  input  [7:0] in_1,
  input  [7:0] in_2,
  output [7:0] out_3,
  output out_4
);

  wire full_adder_1_out_5, full_adder_2_out_5, full_adder_3_out_5, full_adder_4_out_5, full_adder_5_out_5,
       full_adder_6_out_5, full_adder_7_out_5;

  Pull_Resistor pull_resistor_1 (.node(in_1));
  Pull_Resistor pull_resistor_2 (.node(in_2));
  full_adder full_adder_1 (.in_1(in_1[0]), .in_2(in_2[0]), .in_3(1'b0), .out_4(out_3[0]), .out_5(full_adder_1_out_5));
  full_adder full_adder_2 (
    .in_1(in_1[1]), .in_2(in_2[1]), .in_3(full_adder_1_out_5), .out_4(out_3[1]), .out_5(full_adder_2_out_5));
  full_adder full_adder_3 (
    .in_1(in_1[2]), .in_2(in_2[2]), .in_3(full_adder_2_out_5), .out_4(out_3[2]), .out_5(full_adder_3_out_5));
  full_adder full_adder_4 (
    .in_1(in_1[3]), .in_2(in_2[3]), .in_3(full_adder_3_out_5), .out_4(out_3[3]), .out_5(full_adder_4_out_5));
  full_adder full_adder_5 (
    .in_1(in_1[4]), .in_2(in_2[4]), .in_3(full_adder_4_out_5), .out_4(out_3[4]), .out_5(full_adder_5_out_5));
  full_adder full_adder_6 (
    .in_1(in_1[5]), .in_2(in_2[5]), .in_3(full_adder_5_out_5), .out_4(out_3[5]), .out_5(full_adder_6_out_5));
  full_adder full_adder_7 (
    .in_1(in_1[6]), .in_2(in_2[6]), .in_3(full_adder_6_out_5), .out_4(out_3[6]), .out_5(full_adder_7_out_5));
  full_adder full_adder_8 (.in_1(in_1[7]), .in_2(in_2[7]), .in_3(full_adder_7_out_5), .out_4(out_3[7]), .out_5(out_4));
endmodule

module Register_ALU (
);

  wire clk, instruction_regester_1_out_5, instruction_regester_1_out_6, instruction_regester_1_out_7,
       instruction_regester_1_out_9, instruction_regester_1_out_10, instruction_regester_1_out_11,
       instruction_regester_1_out_12, instruction_regester_1_out_13, instruction_regester_1_out_14,
       instruction_regester_1_out_15, instruction_regester_1_out_16, instruction_regester_1_out_17,
       instruction_regester_1_out_18, instruction_regester_1_out_19, instruction_regester_1_out_20,
       instruction_regester_1_out_21, not_1_out;
  wire [1:0] alu_c, instruction_regester_1_out_8;
  wire [7:0] controlled_buffer_1_out, instruction_pointer_1_low, low_register_1_out_6, low_register_2_out_6,
       low_register_3_out_6, multiplexer_1_out;
  wire [8:0] instruction_regester_1_out_4;
  wire [15:0] instruction_pointer_1_out_8;
  wire [15:8] instruction_pointer_1_high_2;

  Instruction_Regester instruction_regester_1 (
    .in_1(alu_c), .in_2(controlled_buffer_1_out), .in_3(clk), .out_4(instruction_regester_1_out_4),
    .out_5(instruction_regester_1_out_5), .out_6(instruction_regester_1_out_6),
    .out_7(instruction_regester_1_out_7), .out_8(instruction_regester_1_out_8),
    .out_9(instruction_regester_1_out_9), .out_10(instruction_regester_1_out_10),
    .out_11(instruction_regester_1_out_11), .out_12(instruction_regester_1_out_12),
    .out_13(instruction_regester_1_out_13), .out_14(instruction_regester_1_out_14),
    .out_15(instruction_regester_1_out_15), .out_16(instruction_regester_1_out_16),
    .out_17(instruction_regester_1_out_17), .out_18(instruction_regester_1_out_18),
    .out_19(instruction_regester_1_out_19), .out_20(instruction_regester_1_out_20),
    .out_21(instruction_regester_1_out_21));
  Clock clock_1 (.out(clk));
  assign controlled_buffer_1_out = instruction_regester_1_out_21 ? 8'h2 : 8'bz;  // Controlled_Buffer controlled_buffer_1
  Pull_Resistor pull_resistor_1 (.node(instruction_regester_1_out_21));
  // Probe on low_register_2_out_6
  // Probe on low_register_1_out_6
  low_register low_register_1 (
    .in_1(clk), .in_3(controlled_buffer_1_out), .out_6(low_register_1_out_6),
    .in_2(instruction_regester_1_out_5));  // open: in_4, out_7, in_5, out_8
  low_register low_register_2 (
    .in_1(clk), .in_3(controlled_buffer_1_out), .in_4(instruction_regester_1_out_6),
    .out_7(controlled_buffer_1_out), .out_6(low_register_2_out_6), .in_2(instruction_regester_1_out_7));  // open: in_5, out_8
  Instruction_Pointer instruction_pointer_1 (
    .in_1(clk), .in_2(instruction_regester_1_out_11), .HIGH_2(instruction_pointer_1_high_2),
    .in_6(instruction_regester_1_out_12), .LOW(instruction_pointer_1_low), .in_3(instruction_pointer_1_low),
    .HIGH(instruction_pointer_1_high_2), .out_8(instruction_pointer_1_out_8),
    .in_5(instruction_regester_1_out_20));  // open: in_7
  Multiplexer #(.select(2), .width(8), .enable("false")) multiplexer_1 (
    .in0(low_register_1_out_6), .in1(low_register_2_out_6), .in2(low_register_3_out_6), .in3({8{1'b0}}),
    .out(multiplexer_1_out), .sel(instruction_regester_1_out_8));
  // Probe on low_register_3_out_6
  low_register low_register_3 (
    .in_1(clk), .in_3(instruction_pointer_1_low), .in_4(instruction_regester_1_out_9),
    .out_7(instruction_pointer_1_low), .out_6(low_register_3_out_6), .in_2(instruction_regester_1_out_10),
    .out_8(instruction_pointer_1_high_2));  // open: in_5
  // Probe on instruction_pointer_1_out_8
  low_register low_register_4 (
    .in_1(clk), .in_3(instruction_pointer_1_low), .in_4(instruction_regester_1_out_13),
    .out_7(instruction_pointer_1_low), .in_2(instruction_regester_1_out_14));  // open: out_6, in_5, out_8
  low_register low_register_5 (
    .in_1(clk), .in_3(instruction_pointer_1_high_2), .in_4(instruction_regester_1_out_15),
    .out_7(instruction_pointer_1_high_2), .in_2(instruction_regester_1_out_16));  // open: out_6, in_5, out_8
  ALU alu_1 (
    .in_1(multiplexer_1_out), .LOW(instruction_pointer_1_high_2), .in_4(instruction_regester_1_out_4),
    .out_6(alu_c), .HIGH(instruction_pointer_1_low), .clk(clk));  // open: in_3
  not not_1 (not_1_out, clk);
  RAM #(.addrWidth(16), .bus("separate")) ram_1 (
    .addr({instruction_pointer_1_high_2, instruction_pointer_1_low}), .din(controlled_buffer_1_out),
    .data(controlled_buffer_1_out), .str(instruction_regester_1_out_17), .sel(instruction_regester_1_out_18),
    .clk(not_1_out), .ld(instruction_regester_1_out_19));  // open: clr
  // Probe on instruction_pointer_1_low
  // Probe on instruction_pointer_1_high_2

  // Notes on the sheet:
  //   Data Bus
  //   AL
  //   AH
  //   Adrdress bus
endmodule

module Instruction_Regester (
  input  [1:0] in_1,
  input  [7:0] in_2,
  input  in_3,
  output [8:0] out_4,
  output out_5,
  output out_6,
  output out_7,
  output [1:0] out_8,
  output out_9,
  output out_10,
  output out_11,
  output out_12,
  output out_13,
  output out_14,
  output out_15,
  output out_16,
  output out_17,
  output out_18,
  output out_19,
  output out_20,
  output out_21
);

  wire d_ff_1_q, d_ff_2_qn, d_ff_3_qn, d_ff_4_qn, IR_RESET, nor_1_out, not_1_out;
  wire [7:0] falling_edge_regester_1_out_4;
  wire [12:10] d_ff_2_q;

  D_Flip_Flop #(.trigger("falling")) d_ff_1 (
    .clk(in_3), .D(IR_RESET), .Q(d_ff_1_q), .reset(not_1_out));  // open: Qn, preset, en
  not not_1 (not_1_out, IR_RESET);
  D_Flip_Flop #(.trigger("falling")) d_ff_2 (
    .clk(in_3), .D(d_ff_2_qn), .Q(d_ff_2_q[10]), .Qn(d_ff_2_qn), .reset(d_ff_1_q));  // open: preset, en
  D_Flip_Flop #(.trigger("falling")) d_ff_3 (
    .clk(d_ff_2_q[10]), .D(d_ff_3_qn), .Q(d_ff_2_q[11]), .Qn(d_ff_3_qn), .reset(d_ff_1_q));  // open: preset, en
  nor nor_1 (nor_1_out, d_ff_2_q[10], d_ff_2_q[11], d_ff_2_q[12]);
  D_Flip_Flop #(.trigger("falling")) d_ff_4 (
    .clk(d_ff_2_q[11]), .D(d_ff_4_qn), .Q(d_ff_2_q[12]), .Qn(d_ff_4_qn), .reset(d_ff_1_q));  // open: preset, en
  falling_edge_regester falling_edge_regester_1 (
    .in_1(nor_1_out), .in_2(in_2), .out_4(falling_edge_regester_1_out_4));  // open: in_3
  ROM #(.addrWidth(13), .dataWidth(28)) rom_1 (
    .addr({d_ff_2_q, falling_edge_regester_1_out_4, in_1}),
    .data({out_21, out_20, IR_RESET, out_19, out_18, out_17, out_16, out_15, out_14, out_13, out_12, out_11, out_10, out_9, out_8, out_7, out_6, out_5, out_4}));  // open: sel

  // Notes on the sheet:
  //   contents of rom_1 (hex, n*v repeats v):
  //   1024*5810000 4*7810200 4*3810841
endmodule

module falling_edge_regester (
  input  in_1,
  input  [7:0] in_2,
  input  in_3,
  output [7:0] out_4
);

  Pull_Resistor pull_resistor_1 (.node(in_2));
  D_Flip_Flop #(.trigger("falling")) d_ff_1 (
    .clk(in_1), .D(in_2[0]), .Q(out_4[0]), .reset(in_3));  // open: Qn, preset, en
  D_Flip_Flop #(.trigger("falling")) d_ff_2 (
    .clk(in_1), .D(in_2[1]), .Q(out_4[1]), .reset(in_3));  // open: Qn, preset, en
  D_Flip_Flop #(.trigger("falling")) d_ff_3 (
    .clk(in_1), .D(in_2[2]), .Q(out_4[2]), .reset(in_3));  // open: Qn, preset, en
  D_Flip_Flop #(.trigger("falling")) d_ff_4 (
    .clk(in_1), .D(in_2[3]), .Q(out_4[3]), .reset(in_3));  // open: Qn, preset, en
  D_Flip_Flop #(.trigger("falling")) d_ff_5 (
    .clk(in_1), .D(in_2[4]), .Q(out_4[4]), .reset(in_3));  // open: Qn, preset, en
  D_Flip_Flop #(.trigger("falling")) d_ff_6 (
    .clk(in_1), .D(in_2[5]), .Q(out_4[5]), .reset(in_3));  // open: Qn, preset, en
  D_Flip_Flop #(.trigger("falling")) d_ff_7 (
    .clk(in_1), .D(in_2[6]), .Q(out_4[6]), .reset(in_3));  // open: Qn, preset, en
  D_Flip_Flop #(.trigger("falling")) d_ff_8 (
    .clk(in_1), .D(in_2[7]), .Q(out_4[7]), .reset(in_3));  // open: Qn, preset, en
endmodule
